# Fritzing sketch Real_bulb_simulation_ Circuit Diagram (saved by Fritzing 0.9.3b)

parts:
  LED1 = LEDs [package=led10mm]
  U1 = ESP8266 NodeMCU LoLin module
  Part4 = Lilypad Battery Connect
  KY-1 = Keyes Relay [package=THT]

nets:
  N1: LED1.A, KY-1.C
  N2: LED1.C, Part4.+
  N3: U1.D0, KY-1.signal
  N4: U1.3V3, KY-1.power
  N5: U1.GND, KY-1.ground
  N6: Part4.-, KY-1.NO

notes:
  240V AC power supply

custom parts:
  LEDs: LEDs Standard schematic elements and footprints for 5mm, 3mm, 1206, and 0603 sized LEDs. 5mm - Spark Fun Electronics SKU : COM-00529 (and others)
  ESP8266 NodeMCU LoLin module: ESP8266 based NodeMCU
  Keyes Relay: The Keyes 5V relay module is suitable for SCM development, home appliance control. It uses a 5V~12V TIL control signal which can control DC / AC signal.
